// Logisim project semaforo_Parpadeo.circ as structural Verilog: 1 circuit, main circuit Semaforo_parpadeo
module Semaforo_parpadeo (
  input  in_1,
  input  A
);

  wire and_1_out, and_2_out, and_3_out, clock_1_out, clock_2_out, d_ff_1_q, d_ff_2_q, d_ff_3_q, d_ff_4_q,
       d_ff_5_q, d_ff_6_q, d_ff_7_q, d_ff_8_q, d_ff_9_q, nand_1_out, nand_2_out, nand_3_out, nand_4_out,
       nand_5_out, nand_6_out, nand_7_out, nand_8_out, nand_9_out, nand_10_out, nand_11_out, nand_12_out,
       nand_13_out, nand_14_out, nand_15_out, nand_16_out, nand_17_out, nand_18_out, nand_19_out,
       nand_20_out, nand_21_out, nand_22_out, nand_23_out, nand_24_out, nor_1_out, nor_2_out, nor_3_out,
       nor_4_out, nor_5_out, nor_6_out, nor_7_out, nor_8_out, nor_9_out, nor_10_out, nor_11_out, nor_12_out,
       nor_13_out, nor_14_out, nor_15_out, nor_16_out, nor_17_out, nor_18_out, nor_19_out, not_1_out,
       not_2_out, not_3_out, not_4_out, not_5_out, not_6_out, not_7_out, not_8_out, not_9_out, not_10_out,
       not_11_out, not_12_out, not_13_out, undriven;

  not not_1 (not_1_out, not_11_out);
  not not_2 (not_2_out, nor_19_out);
  not not_3 (not_3_out, 1'b0);
  not not_4 (not_4_out, 1'b0);
  not not_5 (not_5_out, A);
  nand nand_1 (nand_1_out, 1'b0, not_11_out);
  nand nand_2 (nand_2_out, not_13_out, 1'b1);
  nor nor_1 (nor_1_out, nand_2_out, A);
  nand nand_3 (nand_3_out, not_1_out, nand_2_out);
  nor nor_2 (nor_2_out, not_2_out, 1'b0);
  nor nor_3 (nor_3_out, not_2_out, not_3_out);
  nor nor_4 (nor_4_out, not_4_out, A);
  nand nand_4 (nand_4_out, not_11_out, not_5_out);
  nor nor_5 (nor_5_out, A, nand_1_out);
  nor nor_6 (nor_6_out, not_5_out, 1'b0);
  nand nand_5 (nand_5_out, not_5_out, not_3_out);
  nand nand_6 (nand_6_out, not_5_out, not_13_out);
  nor nor_7 (nor_7_out, nand_3_out, not_2_out);
  nand nand_7 (nand_7_out, nor_2_out, 1'b0);
  nand nand_8 (nand_8_out, nor_3_out, not_4_out);
  nor nor_8 (nor_8_out, nor_4_out, nor_6_out);
  nand nand_9 (nand_9_out, not_1_out, nand_5_out);
  nand nand_10 (nand_10_out, nand_2_out, nand_9_out);
  nand nand_11 (nand_11_out, not_11_out, nand_7_out);
  nand nand_12 (nand_12_out, not_13_out, nand_8_out);
  nand nand_13 (nand_13_out, not_13_out, nand_11_out);
  nand nand_14 (nand_14_out, not_11_out, nand_12_out);
  nand nand_15 (nand_15_out, not_2_out, nand_10_out);
  not not_6 (not_6_out, nand_14_out);
  not not_7 (not_7_out, nand_13_out);
  nor nor_9 (nor_9_out, nand_13_out, not_2_out);
  nor nor_10 (nor_10_out, nand_14_out, not_2_out);
  nand nand_16 (nand_16_out, nor_9_out, nand_4_out);
  nand nand_17 (nand_17_out, nor_10_out, nand_6_out);
  not not_8 (not_8_out, nand_16_out);
  not not_9 (not_9_out, nand_17_out);
  nand nand_18 (nand_18_out, nand_16_out, nand_14_out);
  nand nand_19 (nand_19_out, not_6_out, nand_17_out);
  nor nor_11 (nor_11_out, nor_8_out, nand_18_out);
  nand nand_20 (nand_20_out, nand_19_out, nand_13_out);
  nor nor_12 (nor_12_out, nor_7_out, nor_11_out);
  Clock clock_1 (.out(clock_1_out));
  nand nand_21 (nand_21_out, nor_12_out, nand_15_out);
  nand nand_22 (nand_22_out, nand_21_out, nand_13_out);
  not not_10 (not_10_out, nand_22_out);
  nor nor_13 (nor_13_out, nand_22_out, nor_19_out);
  nand nand_23 (nand_23_out, not_10_out, nor_19_out);
  nor nor_14 (nor_14_out, nor_13_out, nor_5_out);
  nor nor_15 (nor_15_out, nor_1_out, nand_23_out);
  nand nand_24 (nand_24_out, nor_14_out, nand_14_out);
  Clock #(.highDuration(3), .lowDuration(3)) clock_2 (.out(clock_2_out));
  D_Flip_Flop d_ff_1 (.D(nand_24_out), .clk(clock_2_out), .Q(d_ff_1_q), .preset(in_1));  // open: Qn, reset
  D_Flip_Flop d_ff_2 (.D(nor_15_out), .clk(clock_2_out), .Q(d_ff_2_q));  // open: Qn, preset, reset
  D_Flip_Flop d_ff_3 (.D(not_7_out), .clk(clock_2_out), .Q(d_ff_3_q));  // open: Qn, preset, reset
  D_Flip_Flop d_ff_4 (.D(nand_20_out), .clk(clock_2_out), .Q(d_ff_4_q), .preset(in_1));  // open: Qn, reset
  D_Flip_Flop d_ff_5 (.D(not_9_out), .clk(clock_2_out), .Q(d_ff_5_q));  // open: Qn, preset, reset
  D_Flip_Flop d_ff_6 (.D(not_10_out), .clk(clock_2_out), .Q(d_ff_6_q), .reset(in_1));  // open: Qn, preset
  D_Flip_Flop d_ff_7 (.D(nand_21_out), .clk(clock_2_out), .Q(d_ff_7_q), .preset(in_1));  // open: Qn, reset
  D_Flip_Flop d_ff_8 (.D(not_8_out), .clk(clock_2_out), .Q(d_ff_8_q));  // open: Qn, preset, reset
  D_Flip_Flop d_ff_9 (.D(not_6_out), .clk(clock_2_out), .Q(d_ff_9_q), .preset(undriven));  // open: Qn, reset
  not not_11 (not_11_out, d_ff_7_q);
  and and_1 (and_1_out, d_ff_8_q, clock_1_out);
  and and_2 (and_2_out, d_ff_2_q, clock_1_out);
  nor nor_16 (nor_16_out, d_ff_2_q, d_ff_5_q);
  nor nor_17 (nor_17_out, d_ff_1_q, d_ff_8_q);
  LED WR (.in(d_ff_1_q));
  LED WY (.in(and_2_out));
  LED WG (.in(d_ff_3_q));
  not not_12 (not_12_out, nor_16_out);
  nor nor_18 (nor_18_out, d_ff_5_q, nor_17_out);
  nor nor_19 (nor_19_out, not_12_out, d_ff_8_q);
  not not_13 (not_13_out, nor_18_out);
  and and_3 (and_3_out, d_ff_5_q, clock_1_out);
  LED NR (.in(d_ff_7_q));
  LED NY (.in(and_1_out));
  LED NG (.in(d_ff_9_q));
  LED ER (.in(d_ff_4_q));
  LED EY (.in(and_3_out));
  LED EG (.in(d_ff_6_q));

  // Notes on the sheet:
  //   S'1
  //   Start
  //   S'2
  //   S'3
  //   S1
  //   WEAST
  //   S3
  //   S2
  //   NORTH
  //   EAST
endmodule
